// Logisim project Animations.circ as structural Verilog: 2 circuits, main circuit animation
module animation (
  input  in_1
);

  wire Clear, Clock, clock_1_out, comparator_1_eq, not_1_out;
  wire [11:0] counter_1_q, divider_1_rem;
  wire [15:0] _00, _01, _02, _03, _04, _05, _06, _07, _08, _09, _10, _11, _12, _13, _14, _15, rom_1_data,
       shift_register_1_q0, shift_register_1_q1, shift_register_1_q2, shift_register_1_q3,
       shift_register_1_q4, shift_register_1_q5, shift_register_1_q6, shift_register_1_q7,
       shift_register_1_q8, shift_register_1_q9, shift_register_1_q10, shift_register_1_q11,
       shift_register_1_q12, shift_register_1_q13, shift_register_1_q14, shift_register_1_q15;

  Clock clock_1 (.out(clock_1_out));
  Button button_1 (.out(Clear));
  // Probe on counter_1_q
  Counter #(.width(12), .max('h87)) counter_1 (
    .count(in_1), .Q(counter_1_q), .clk(Clock), .clr(Clear));  // open: load, D, carry
  and and_1 (Clock, clock_1_out, in_1);
  // Probe on divider_1_rem
  Divider #(.width(12)) divider_1 (.a(counter_1_q), .b(12'h11), .rem(divider_1_rem));  // open: out, upper
  DotMatrix #(.matrixcols(16), .matrixrows(16)) dotmatrix_1 (
    .col0(_15), .col1(_14), .col2(_13), .col3(_12), .col4(_11), .col5(_10), .col6(_09), .col7(_08),
    .col8(_07), .col9(_06), .col10(_05), .col11(_04), .col12(_03), .col13(_02), .col14(_01), .col15(_00));
  Comparator #(.width(12)) comparator_1 (.a(divider_1_rem), .b({12{1'b0}}), .eq(comparator_1_eq));  // open: gt, lt
  ROM #(.addrWidth(12), .dataWidth(16)) rom_1 (.addr(counter_1_q), .data(rom_1_data));  // open: sel
  LED led_1 (.in(comparator_1_eq));
  not not_1 (not_1_out, comparator_1_eq);
  Shift_Register #(.width(16), .length(16)) shift_register_1 (
    .shift(not_1_out), .in(rom_1_data), .clk(Clock), .clr(Clear), .q0(shift_register_1_q0),
    .q1(shift_register_1_q1), .q2(shift_register_1_q2), .q3(shift_register_1_q3), .q4(shift_register_1_q4),
    .q5(shift_register_1_q5), .q6(shift_register_1_q6), .q7(shift_register_1_q7), .q8(shift_register_1_q8),
    .q9(shift_register_1_q9), .q10(shift_register_1_q10), .q11(shift_register_1_q11),
    .q12(shift_register_1_q12), .q13(shift_register_1_q13), .q14(shift_register_1_q14),
    .q15(shift_register_1_q15));  // open: out, load, d0, d1, d2, d3, d4, d5, d6, d7, d8, d9, d10, d11, d12, d13, d14, d15
  Shift_Register #(.width(16), .length(16)) shift_register_2 (
    .shift(1'b0), .clk(Clock), .load(comparator_1_eq), .clr(Clear), .d0(shift_register_1_q0), .q0(_00),
    .d1(shift_register_1_q1), .q1(_01), .d2(shift_register_1_q2), .q2(_02), .d3(shift_register_1_q3),
    .q3(_03), .d4(shift_register_1_q4), .q4(_04), .d5(shift_register_1_q5), .q5(_05),
    .d6(shift_register_1_q6), .q6(_06), .d7(shift_register_1_q7), .q7(_07), .d8(shift_register_1_q8),
    .q8(_08), .d9(shift_register_1_q9), .q9(_09), .d10(shift_register_1_q10), .q10(_10),
    .d11(shift_register_1_q11), .q11(_11), .d12(shift_register_1_q12), .q12(_12), .d13(shift_register_1_q13),
    .q13(_13), .d14(shift_register_1_q14), .q14(_14), .d15(shift_register_1_q15), .q15(_15));  // open: in, out

  // Other names for the same wires on the sheet: On_Off = in_1

  // Notes on the sheet:
  //   256Hz
  //   contents of rom_1 (hex, n*v repeats v):
  //   0 ff 7fe c7c 1bbe 383f 7c7f 7fff 7ffc 7c7c 7bbf 783f 3c7f 1ffe ffc 7fe ff 0 fe 7ff c7f 1bbe 383c
  //   7c7e 7fff 7fff 7c7f 7bbf 783e 3c7c 1ffe fff 7ff fe 0 ff 7fe c7c 1bbe 383f 7c7f 7fff 7ffc 7c7c 7bbf
  //   783f 3c7f 1ffe ffc 7fe ff 0 fe 7ff c7f 1bbe 383c 7c7e 7fff 7fff 7c7f 7bbf 783e 3c7c 1ffe fff 7ff fe
  //   0 ff 7fe c7c 183e 3bbf 7c7f 7fff 7ffc 7c7c 783f 7bbf 3c7f 1ffe ffc 7fe ff 0 fe 7ff c7f 183e 3bbc
  //   7c7e 7fff 7fff 7c7f 783f 7bbe 3c7c 1ffe fff 7ff fe 0 ff 7fe c7c 183e 3bbf 7c7f 7fff 7ffc 7c7c 783f
  //   7bbf 3c7f 1ffe ffc 7fe ff 0 fe 7ff c7f 183e 3bbc 7c7e 7fff 7fff 7c7f 783f 7bbe 3c7c 1ffe fff 7ff fe
  //   1
  //   Prof.: Santiago Sinezio
  //   Copyrigth (c) 2020 David Gomesh
  //   Disciplina: Org. e Arq. de Computadores. 
  //   IFMA - Monte Castelo
  //   Animations
endmodule

module details (
  input  in_1
);

  wire Clear, Clock, clock_1_out, comparator_1_eq, not_1_out;
  wire [1:0] _00, _01, _02, _03, _04, _05, _06, _07, rom_1_data, shift_register_1_q0, shift_register_1_q1,
       shift_register_1_q2, shift_register_1_q3, shift_register_1_q4, shift_register_1_q5,
       shift_register_1_q6, shift_register_1_q7;
  wire [4:0] counter_1_q, divider_1_rem;

  Clock clock_1 (.out(clock_1_out));
  Button button_1 (.out(Clear));
  Counter #(.width(5), .max('h1a)) counter_1 (
    .count(in_1), .Q(counter_1_q), .clk(Clock), .clr(Clear));  // open: load, D, carry
  and and_1 (Clock, clock_1_out, in_1);
  Divider #(.width(5)) divider_1 (.a(counter_1_q), .b(5'b01001), .rem(divider_1_rem));  // open: out, upper
  DotMatrix #(.matrixcols(8), .matrixrows(2)) dotmatrix_1 (
    .col0(_07), .col1(_06), .col2(_05), .col3(_04), .col4(_03), .col5(_02), .col6(_01), .col7(_00));
  Comparator #(.width(5)) comparator_1 (.a(divider_1_rem), .b({5{1'b0}}), .eq(comparator_1_eq));  // open: gt, lt
  ROM #(.addrWidth(5), .dataWidth(2)) rom_1 (.addr(counter_1_q), .data(rom_1_data));  // open: sel
  not not_1 (not_1_out, comparator_1_eq);
  Shift_Register #(.width(2)) shift_register_1 (
    .shift(not_1_out), .in(rom_1_data), .clk(Clock), .clr(Clear), .q0(shift_register_1_q0),
    .q1(shift_register_1_q1), .q2(shift_register_1_q2), .q3(shift_register_1_q3), .q4(shift_register_1_q4),
    .q5(shift_register_1_q5), .q6(shift_register_1_q6), .q7(shift_register_1_q7));  // open: out, load, d0, d1, d2, d3, d4, d5, d6, d7
  Shift_Register #(.width(2)) shift_register_2 (
    .shift(1'b0), .clk(Clock), .load(comparator_1_eq), .clr(Clear), .d0(shift_register_1_q0), .q0(_00),
    .d1(shift_register_1_q1), .q1(_01), .d2(shift_register_1_q2), .q2(_02), .d3(shift_register_1_q3),
    .q3(_03), .d4(shift_register_1_q4), .q4(_04), .d5(shift_register_1_q5), .q5(_05),
    .d6(shift_register_1_q6), .q6(_06), .d7(shift_register_1_q7), .q7(_07));  // open: in, out

  // Other names for the same wires on the sheet: On_Off = in_1

  // Notes on the sheet:
  //   contents of rom_1 (hex, n*v repeats v):
  //   0 8*1 0 8*2 0 8*3
endmodule
